# Fritzing sketch 03_spinMotorSpin (saved by Fritzing 0.8.7b)
breadboards: 1

parts:
  Composants1 = Arduino Uno (Rev3)
  Q1 = NPN-Transistor [package="TO92 [THT]"]
  R1 = Resistor [tolerance=±5% resistance=220 package=THT]
  D1 = Diode [package=diode-1n4001]
  M2 = DC Motor

nets:
  N1: Composants1.D9_PWM, R1.Pin_1
  N2: Composants1.5V, D1.A, M2.pin_2
  N3: Composants1.GND, Q1.E
  N4: Q1.B, R1.Pin_0
  N5: Q1.C, D1.C, M2.pin_1
